// Logisim project 2BitBinaryCounter.circ as structural Verilog: 1 circuit, main circuit main
module main (
  input  X
);

  wire and_1_out, B_q, clock_1_out;

  and and_1 (and_1_out, X, B_q);
  J_K_Flip_Flop A (.J(and_1_out), .clk(clock_1_out), .K(and_1_out));  // open: Q, Qn, preset, en, reset
  J_K_Flip_Flop B (.J(X), .clk(clock_1_out), .K(X), .Q(B_q));  // open: Qn, preset, en, reset
  Clock clock_1 (.out(clock_1_out));
endmodule
