// Logisim project FullAdder.circ as structural Verilog: 1 circuit, main circuit main
module main (
  input  X,
  input  Y,
  output S,
  output Q,
  output out_5
);

  wire adder_1_cout, clock_1_out;

  not not_1 (out_5, adder_1_cout);
  Adder #(.width(1)) adder_1 (.a(X), .b(Y), .out(S), .cin(Q), .cout(adder_1_cout));
  D_Flip_Flop d_ff_1 (.clk(clock_1_out), .D(out_5), .Q(Q));  // open: Qn, preset, en, reset
  Clock clock_1 (.out(clock_1_out));
endmodule
