// Logisim project SimplifiedAdder.circ as structural Verilog: 1 circuit, main circuit main
module main (
  input  Z,
  input  Y,
  input  X,
  output Sum,
  output Carry
);

  wire and_1_out, and_2_out, NOT_X_out, NOT_Y_out, NOT_Z_out, xor_1_out, xor_2_out;

  not NOT_X (NOT_X_out, Y);
  not NOT_Y (NOT_Y_out, X);
  not NOT_Z (NOT_Z_out, Z);
  xor xor_1 (xor_1_out, X, Y);
  xor xor_2 (xor_2_out, X, Y);
  and and_1 (and_1_out, X, Y);
  xor xor_3 (Sum, xor_1_out, Z);
  and and_2 (and_2_out, xor_2_out, Z);
  or or_1 (Carry, and_2_out, and_1_out);
endmodule
