// Logisim project XYZtoABC.circ as structural Verilog: 1 circuit, main circuit main
module main (
  input  X,
  input  Y,
  input  Z,
  output A,
  output B,
  output C
);

  wire and_1_out, and_2_out, and_3_out, and_4_out, and_5_out, and_6_out, not_1_out, not_2_out, not_3_out;

  not not_1 (not_1_out, X);
  not not_2 (not_2_out, Y);
  not not_3 (not_3_out, Z);
  and and_1 (and_1_out, X, Z);
  and and_2 (and_2_out, not_1_out, not_2_out);
  and and_3 (and_3_out, X, Y, Z);
  and and_4 (and_4_out, X, not_2_out, not_3_out);
  and and_5 (and_5_out, not_1_out, Z);
  and and_6 (and_6_out, X, not_3_out);
  or u_A (A, Y, and_1_out);
  or u_B (B, and_2_out, and_3_out, and_4_out);
  or u_C (C, and_5_out, and_6_out);
endmodule
