// Logisim project XYtoABandZ.circ as structural Verilog: 1 circuit, main circuit main
module main (
  input  X,
  input  Y,
  output Z
);

  wire A_q, and_1_out, and_2_out, and_3_out, and_4_out, and_5_out, and_6_out, and_7_out, B_q, clock_1_out,
       not_1_out, not_2_out, or_2_out, or_3_out, or_4_out;

  not not_1 (not_1_out, X);
  not not_2 (not_2_out, Y);
  and and_1 (and_1_out, X, not_2_out);
  and and_2 (and_2_out, not_1_out, Y);
  and and_3 (and_3_out, Y, B_q);
  and and_4 (and_4_out, B_q, not_1_out);
  and and_5 (and_5_out, X, Y);
  and and_6 (and_6_out, B_q, Y);
  and and_7 (and_7_out, not_1_out, A_q);
  or or_1 (Z, Y, and_1_out);
  Clock clock_1 (.out(clock_1_out));
  or or_2 (or_2_out, and_2_out, and_3_out);
  or or_3 (or_3_out, and_4_out, and_5_out);
  or or_4 (or_4_out, and_6_out, and_7_out);
  D_Flip_Flop A (.clk(clock_1_out), .D(or_2_out), .Q(A_q));  // open: Qn, preset, en, reset
  J_K_Flip_Flop B (.J(or_3_out), .clk(clock_1_out), .K(or_4_out), .Q(B_q));  // open: Qn, preset, en, reset
endmodule
